// Logisim project BusDebugger.circ as structural Verilog: 1 circuit, main circuit main
module main (
);

  wire demultiplexer_1_out0, demultiplexer_1_out1, demultiplexer_1_out2, demultiplexer_1_out3,
       demultiplexer_1_out4, demultiplexer_1_out5, demultiplexer_1_out6, demultiplexer_1_out7, NE555_out,
       not_1_out, not_2_out, not_3_out, not_4_out, not_5_out, not_6_out, not_7_out, not_8_out, undriven,
       undriven_2, undriven_3, undriven_4, undriven_5, undriven_6, undriven_7, undriven_8;
  wire [2:0] _74LS163_q;
  wire [3:0] multiplexer_1_out;
  wire [6:0] controlled_buffer_2_out, controlled_buffer_3_out, controlled_buffer_4_out,
       controlled_buffer_5_out, controlled_buffer_6_out, controlled_buffer_7_out, controlled_buffer_8_out;
  wire [7:0] AT28C16_data, controlled_buffer_1_out, not_9_out;

  not not_1 (not_1_out, not_9_out[0]);
  assign controlled_buffer_1_out = not_1_out ? AT28C16_data : 8'bz;  // Controlled_Buffer controlled_buffer_1
  _7_Segment_Display u_7_segment_display_1 (
    .g(controlled_buffer_1_out[0]), .f(controlled_buffer_1_out[1]), .a(controlled_buffer_1_out[6]),
    .b(controlled_buffer_1_out[5]), .e(controlled_buffer_1_out[2]), .d(controlled_buffer_1_out[3]),
    .c(controlled_buffer_1_out[4]), .dp(undriven));
  not not_2 (not_2_out, not_9_out[1]);
  assign {controlled_buffer_1_out[7], controlled_buffer_2_out} = not_2_out ? AT28C16_data : 8'bz;  // Controlled_Buffer controlled_buffer_2
  _7_Segment_Display u_7_segment_display_2 (
    .g(controlled_buffer_2_out[0]), .f(controlled_buffer_2_out[1]), .a(controlled_buffer_2_out[6]),
    .b(controlled_buffer_2_out[5]), .e(controlled_buffer_2_out[2]), .d(controlled_buffer_2_out[3]),
    .c(controlled_buffer_2_out[4]), .dp(undriven_2));
  not not_3 (not_3_out, not_9_out[2]);
  assign {controlled_buffer_1_out[7], controlled_buffer_3_out} = not_3_out ? AT28C16_data : 8'bz;  // Controlled_Buffer controlled_buffer_3
  _7_Segment_Display u_7_segment_display_3 (
    .g(controlled_buffer_3_out[0]), .f(controlled_buffer_3_out[1]), .a(controlled_buffer_3_out[6]),
    .b(controlled_buffer_3_out[5]), .e(controlled_buffer_3_out[2]), .d(controlled_buffer_3_out[3]),
    .c(controlled_buffer_3_out[4]), .dp(undriven_3));
  not not_4 (not_4_out, not_9_out[3]);
  assign {controlled_buffer_1_out[7], controlled_buffer_4_out} = not_4_out ? AT28C16_data : 8'bz;  // Controlled_Buffer controlled_buffer_4
  _7_Segment_Display u_7_segment_display_4 (
    .g(controlled_buffer_4_out[0]), .f(controlled_buffer_4_out[1]), .a(controlled_buffer_4_out[6]),
    .b(controlled_buffer_4_out[5]), .e(controlled_buffer_4_out[2]), .d(controlled_buffer_4_out[3]),
    .c(controlled_buffer_4_out[4]), .dp(undriven_4));
  Multiplexer #(.enable("false"), .select(3)) multiplexer_1 (
    .in0(1'b0), .in1(1'b1), .in2(1'b0), .in3(1'b1), .in4(1'b0), .in5(1'b1), .in6(1'b0), .in7(1'b1),
    .out(multiplexer_1_out[0]), .sel(_74LS163_q));
  Multiplexer #(.enable("false"), .select(3)) multiplexer_2 (
    .in0(1'b0), .in1(1'b0), .in2(1'b1), .in3(1'b1), .in4(1'b1), .in5(1'b1), .in6(1'b0), .in7(1'b0),
    .out(multiplexer_1_out[1]), .sel(_74LS163_q));
  Multiplexer #(.enable("false"), .select(3)) multiplexer_3 (
    .in0(1'b0), .in1(1'b0), .in2(1'b0), .in3(1'b0), .in4(1'b0), .in5(1'b0), .in6(1'b1), .in7(1'b1),
    .out(multiplexer_1_out[2]), .sel(_74LS163_q));
  Multiplexer #(.enable("false"), .select(3)) multiplexer_4 (
    .in0(1'b0), .in1(1'b0), .in2(1'b0), .in3(1'b0), .in4(1'b1), .in5(1'b1), .in6(1'b1), .in7(1'b1),
    .out(multiplexer_1_out[3]), .sel(_74LS163_q));
  Clock NE555 (.out(NE555_out));
  not not_5 (not_5_out, not_9_out[4]);
  assign {controlled_buffer_1_out[7], controlled_buffer_5_out} = not_5_out ? AT28C16_data : 8'bz;  // Controlled_Buffer controlled_buffer_5
  _7_Segment_Display u_7_segment_display_5 (
    .g(controlled_buffer_5_out[0]), .f(controlled_buffer_5_out[1]), .a(controlled_buffer_5_out[6]),
    .b(controlled_buffer_5_out[5]), .e(controlled_buffer_5_out[2]), .d(controlled_buffer_5_out[3]),
    .c(controlled_buffer_5_out[4]), .dp(undriven_5));
  Counter #(.max('h7), .width(3)) _74LS163 (.Q(_74LS163_q), .clk(NE555_out));  // open: load, D, count, carry, clr
  not not_6 (not_6_out, not_9_out[5]);
  assign {controlled_buffer_1_out[7], controlled_buffer_6_out} = not_6_out ? AT28C16_data : 8'bz;  // Controlled_Buffer controlled_buffer_6
  _7_Segment_Display u_7_segment_display_6 (
    .g(controlled_buffer_6_out[0]), .f(controlled_buffer_6_out[1]), .a(controlled_buffer_6_out[6]),
    .b(controlled_buffer_6_out[5]), .e(controlled_buffer_6_out[2]), .d(controlled_buffer_6_out[3]),
    .c(controlled_buffer_6_out[4]), .dp(undriven_6));
  not not_7 (not_7_out, not_9_out[6]);
  assign {controlled_buffer_1_out[7], controlled_buffer_7_out} = not_7_out ? AT28C16_data : 8'bz;  // Controlled_Buffer controlled_buffer_7
  _7_Segment_Display u_7_segment_display_7 (
    .g(controlled_buffer_7_out[0]), .f(controlled_buffer_7_out[1]), .a(controlled_buffer_7_out[6]),
    .b(controlled_buffer_7_out[5]), .e(controlled_buffer_7_out[2]), .d(controlled_buffer_7_out[3]),
    .c(controlled_buffer_7_out[4]), .dp(undriven_7));
  ROM #(.addrWidth(11)) AT28C16 (.addr({{7{1'b0}}, multiplexer_1_out}), .data(AT28C16_data));
  Demultiplexer #(.enable("false"), .select(3)) demultiplexer_1 (
    .out0(demultiplexer_1_out0), .out1(demultiplexer_1_out1), .out2(demultiplexer_1_out2),
    .out3(demultiplexer_1_out3), .out4(demultiplexer_1_out4), .out5(demultiplexer_1_out5),
    .out6(demultiplexer_1_out6), .out7(demultiplexer_1_out7), .in(1'b1), .sel(_74LS163_q));
  not not_8 (not_8_out, not_9_out[7]);
  assign {controlled_buffer_1_out[7], controlled_buffer_8_out} = not_8_out ? AT28C16_data : 8'bz;  // Controlled_Buffer controlled_buffer_8
  _7_Segment_Display u_7_segment_display_8 (
    .g(controlled_buffer_8_out[0]), .f(controlled_buffer_8_out[1]), .a(controlled_buffer_8_out[6]),
    .b(controlled_buffer_8_out[5]), .e(controlled_buffer_8_out[2]), .d(controlled_buffer_8_out[3]),
    .c(controlled_buffer_8_out[4]), .dp(undriven_8));
  not not_9 (not_9_out[0], demultiplexer_1_out0);
  not not_10 (not_9_out[1], demultiplexer_1_out1);
  not not_11 (not_9_out[2], demultiplexer_1_out2);
  not not_12 (not_9_out[3], demultiplexer_1_out3);
  not not_13 (not_9_out[4], demultiplexer_1_out4);
  not not_14 (not_9_out[5], demultiplexer_1_out5);
  not not_15 (not_9_out[6], demultiplexer_1_out6);
  not not_16 (not_9_out[7], demultiplexer_1_out7);
  LED #(.active("false")) led_1 (.in(controlled_buffer_1_out[7]));

  // Notes on the sheet:
  //   4x 74LS151
  //   RESET
  //   READ
  //   contents of AT28C16 (hex, n*v repeats v):
  //   16*7f 7e 30 6d 79 33 5b 5f 70 7f 7b 77 1f 4e 3d 4f 47 16*ff fe b0 ed f9 b3 db df f0 ff fb f7 9f ce
  //   bd cf c7 1984*ff
  //   74LS137
  //   WRITE
endmodule
